// Logisim project LAB1.circ as structural Verilog: 1 circuit, main circuit main
module main (
  input  in_1,
  input  in_2,
  input  in_3,
  input  in_4,
  input  in_5,
  input  in_6,
  input  in_7,
  input  in_8,
  input  in_9,
  input  A,
  input  in_11,
  input  B,
  input  in_13,
  input  C,
  input  in_15,
  input  D,
  input  in_17,
  input  in_18,
  input  A_2,
  input  in_20,
  input  B_2,
  input  C_2,
  output out_23,
  output out_24,
  output out_25,
  output out_26,
  output out_27,
  output out_28,
  output out_29,
  output out_30,
  output A_o,
  output B_o,
  output C_o,
  output out_34,
  output D_o,
  output out_36,
  output out_37,
  output F
);

  wire and_2_out, clock_1_out, clock_2_out, clock_3_out;

  and and_1 (out_24, in_1, in_3);
  or or_1 (out_27, in_4, in_6);
  not not_1 (out_29, in_7);
  nand nand_1 (out_30, in_8, in_9);
  nor nor_1 (out_34, in_11, in_13);
  xor xor_1 (out_36, in_15, in_17);
  xnor xnor_1 (out_37, in_18, in_20);
  Clock clock_1 (.out(clock_1_out));
  Clock clock_2 (.out(clock_2_out));
  Clock clock_3 (.out(clock_3_out));
  D_Flip_Flop d_ff_1 (.clk(clock_1_out), .D(in_2), .Q(out_23), .Qn(out_25), .en(1'b1));  // open: preset, reset
  D_Flip_Flop #(.trigger("high")) d_ff_2 (
    .clk(clock_2_out), .D(in_5), .Q(out_26), .Qn(out_28), .en(1'b1));  // open: preset, reset
  Register #(.width(4)) register_1 (
    .D({D, C, B, A}), .en(1'b1), .Q({D_o, C_o, B_o, A_o}), .clk(clock_3_out));  // open: clr
  and and_2 (and_2_out, A_2, B_2);
  or or_2 (F, and_2_out, C_2);

  // Notes on the sheet:
  //   AND
  //   OR
  //   NOT
  //   NAND
  //   NOR
  //   XOR
  //   XNOR
  //   clock
  //   ngo vao
  //   hang so
  //   thanh ghi
  //   ngo ra
endmodule
