// Logisim project LAB02.circ as structural Verilog: 1 circuit, main circuit main
module main (
  input  [1:0] in_1,
  input  [7:0] A,
  input  [7:0] B,
  input  [7:0] A_2,
  input  [7:0] B_2,
  input  [2:0] in_6,
  input  [1:0] in_7,
  input  [7:0] in_8,
  input  [1:0] ADD,
  input  E,
  output [7:0] S,
  output [7:0] S_2,
  output [7:0] out_13
);

  wire clock_1_out, decoder_1_out0, decoder_1_out1, decoder_1_out2, decoder_1_out3;
  wire [7:0] adder_1_out, adder_2_out, adder_3_out, and_1_out, and_2_out, nand_1_out, not_1_out, or_1_out,
       register_1_q, register_2_q, register_3_q, register_4_q, subtractor_1_out, subtractor_2_out,
       subtractor_3_out, xor_1_out;

  Decoder #(.select(2)) decoder_1 (
    .out0(decoder_1_out0), .out1(decoder_1_out1), .out2(decoder_1_out2), .out3(decoder_1_out3), .sel(ADD),
    .en(E));
  Clock clock_1 (.out(clock_1_out));
  Adder adder_1 (.a(A), .b(B), .out(adder_1_out));  // open: cin, cout
  Subtractor subtractor_1 (.a(A), .b(B), .out(subtractor_1_out));  // open: bin, bout
  assign and_1_out = A & B;  // AND_Gate and_1, 8 bits wide
  assign nand_1_out = ~(A & B);  // NAND_Gate nand_1, 8 bits wide
  Adder adder_2 (.a(A_2), .b(B_2), .out(adder_2_out));  // open: cin, cout
  Adder adder_3 (.a(A_2), .b(8'h1), .out(adder_3_out));  // open: cin, cout
  Subtractor subtractor_2 (.a(A_2), .b(B_2), .out(subtractor_2_out));  // open: bin, bout
  Subtractor subtractor_3 (.a(A_2), .b(8'h1), .out(subtractor_3_out));  // open: bin, bout
  assign and_2_out = A_2 & B_2;  // AND_Gate and_2, 8 bits wide
  assign or_1_out = A_2 | B_2;  // OR_Gate or_1, 8 bits wide
  assign not_1_out = ~A_2;  // NOT_Gate not_1, 8 bits wide
  assign xor_1_out = A_2 ^ B_2;  // XOR_Gate xor_1, 8 bits wide
  Register register_1 (.D(in_8), .en(decoder_1_out0), .Q(register_1_q), .clk(clock_1_out));  // open: clr
  Register register_2 (.D(in_8), .en(decoder_1_out1), .Q(register_2_q), .clk(clock_1_out));  // open: clr
  Register register_3 (.D(in_8), .en(decoder_1_out2), .Q(register_3_q), .clk(clock_1_out));  // open: clr
  Register register_4 (.D(in_8), .en(decoder_1_out3), .Q(register_4_q), .clk(clock_1_out));  // open: clr
  Multiplexer #(.select(2), .width(8)) multiplexer_1 (
    .in0(adder_1_out), .in1(subtractor_1_out), .in2(and_1_out), .in3(nand_1_out), .out(S), .sel(in_1));  // open: en
  Multiplexer #(.select(3), .width(8)) multiplexer_2 (
    .in0(adder_2_out), .in1(adder_3_out), .in2(subtractor_2_out), .in3(subtractor_3_out), .in4(and_2_out),
    .in5(or_1_out), .in6(not_1_out), .in7(xor_1_out), .out(S_2), .sel(in_6));  // open: en
  Multiplexer #(.select(2), .width(8)) multiplexer_3 (
    .in0(register_1_q), .in1(register_2_q), .in2(register_3_q), .in3(register_4_q), .out(out_13), .sel(in_7));  // open: en
endmodule
